# Fritzing sketch GPS-Speedometer (saved by Fritzing 0.9.4)

parts:
  Part1 = Arduino Uno (Rev3)
  U2 = D2523T [package=em406]
  U3 = 7-SEGMENT-4DIGIT [package=7-segment-4digit-youngsun]  # not connected
  U4 = 7-SEGMENT-4DIGIT [package=7-segment-4digit-youngsun]
  microSD1 = MicroSD Card Module

nets:
  N1: Part1.D8, U2.TX
  N2: Part1.D9_PWM, U2.RX
  N3: Part1.D10_PWM/SS, microSD1.SCK
  N4: Part1.D11_PWM/MOSI, microSD1.MOSI
  N5: Part1.D12/MISO, microSD1.MISO
  N6: Part1.D4, microSD1.CS
  N7: Part1.D5_PWM, U4.15
  N8: Part1.D7, U4.9
  3V3: Part1.3V3, U2.VIN
  5V: Part1.5V, U4.7, microSD1.VCC
  GND: Part1.GND, U2.GND, U4.8, microSD1.GND

notes:
  CS
  CLK
  DIN
  GPS TX
  GPS RX
